# Fritzing sketch montage (saved by Fritzing 0.9.6b)
breadboards: 1

parts:
  Composant1 = Arduino Nano (Rev3.0)
  M1 = gear-motor  # not connected
  M2 = gear-motor  # not connected
  L298N1 = L298N DC motor driver
  S1 = Momentary Switch [package=ksa_sealed_tac_switch]
  S2 = Momentary Switch [package=ksa_sealed_tac_switch]
  VCC1 = Battery block 9V

nets:
  N1: Composant1.D3, S1.3
  N2: Composant1.D4, S2.3
  N3: Composant1.D6, L298N1.IN4
  N4: Composant1.D7, L298N1.IN3
  N5: Composant1.D8, L298N1.IN2
  N6: Composant1.D9, L298N1.IN1
  N7: Composant1.D10, L298N1.ENA
  N8: Composant1.D11/MOSI, L298N1.ENB
  N9: Composant1.GND, S1.4, S2.4, VCC1.-

custom parts:
  L298N DC motor driver: 2x DC motor driver with 78M05 positive voltage regulator (7..35 V) L298N: max 46 V, 2 A Set 5 V Enable jumper to enable 5 V regultor (needed for the L298N) and +5 V output at screw terminal or supply external +5 V at screw terminal Set ENA and/or ENB to +5 V to enable motor permanently or supply ENA and/or ENB with PWM signal IN1 and IN2 set rotation directory for motor A (OUT1/OUT2) IN2 and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
